# Fritzing sketch sketch (saved by Fritzing 0.9.3b)

parts:
  MH-ET_LIVE_ESP32_DEVKIT1 = MH-ET LIVE ESP32 DEVKIT 38 pins
  U1 = XD-RF-5V [package=THT]
  R1 = Resistor [tolerance=±1% resistance=10k package="2512 [SMD]"]
  R2 = Resistor [tolerance=±1% resistance=20k package="2512 [SMD]"]

nets:
  N1: MH-ET_LIVE_ESP32_DEVKIT1.IO27, R1.Pin_1, R2.Pin_0
  GND: MH-ET_LIVE_ESP32_DEVKIT1.GND, U1.GND, R2.Pin_1
  5V: MH-ET_LIVE_ESP32_DEVKIT1.5V, U1.VCC
  N2: U1.DATA, R1.Pin_0

notes:
  MX-RM-5V
  R1 - 10kOhm
  R2 - 20kOhm

custom parts:
  MH-ET LIVE ESP32 DEVKIT 38 pins: http://mh.nodebb.com/topic/2/mh-et-live-esp32-devkit
  XD-RF-5V: This is 433Mhz RF transmitter with receiver kit for Arduino ARM MCU wireless Application environment: Remote control switch, receiver module, motorcycles, automobile anti-theft products, home security products, electric doors, shutter doors, windows, remote control socket, remote control LED, remote audio remote control electric doors, garage door remote control, remote control retractable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
