# Fritzing sketch sketch (saved by Fritzing 0.9.3b)

parts:
  MH-ET_LIVE_ESP32_DEVKIT1 = MH-ET LIVE ESP32 DEVKIT 38 pins
  U1 = XD-RF-5V [package=THT]
  R1 = Resistor [tolerance=±1% resistance=10k package="2512 [SMD]"]
  R2 = Resistor [tolerance=±1% resistance=20k package="2512 [SMD]"]
  LED1 = RGB LED (com. cathode, rgb) [package="5 mm [THT]"]
  R3 = Resistor [tolerance=±1% resistance=330 package="2512 [SMD]"]
  R4 = Resistor [tolerance=±1% resistance=220 package="2512 [SMD]"]
  R5 = Resistor [tolerance=±1% resistance=220 package="2512 [SMD]"]
  U2 = FS1000A - 433Mhz RF Transmitter [package=THT]

nets:
  N1: MH-ET_LIVE_ESP32_DEVKIT1.IO27, R1.Pin_1, R2.Pin_0
  N2: MH-ET_LIVE_ESP32_DEVKIT1.IO14, U2.DATA
  GND: MH-ET_LIVE_ESP32_DEVKIT1.GND#58, U1.GND, R2.Pin_1, U2.GND
  VCC: MH-ET_LIVE_ESP32_DEVKIT1.5V, U1.VCC, U2.VCC
  N3: MH-ET_LIVE_ESP32_DEVKIT1.IO21, R5.Pin_0
  N4: MH-ET_LIVE_ESP32_DEVKIT1.GND#70, LED1.common_cathode
  N5: MH-ET_LIVE_ESP32_DEVKIT1.IO19, R4.Pin_0
  N6: MH-ET_LIVE_ESP32_DEVKIT1.IO18, R3.Pin_0
  N7: U1.DATA, R1.Pin_0
  N8: LED1.red_anode, R3.Pin_1
  N9: LED1.green_anode, R4.Pin_1
  N10: LED1.blue_anode, R5.Pin_1

notes:
  MX-RM-5V
  10kOhm
  20kOhm
  Red - 330 Ohm
  Green & Blue
  220 Ohm
  RGB Led
  (common cathode)

custom parts:
  MH-ET LIVE ESP32 DEVKIT 38 pins: http://mh.nodebb.com/topic/2/mh-et-live-esp32-devkit
  XD-RF-5V: This is 433Mhz RF transmitter with receiver kit for Arduino ARM MCU wireless Application environment: Remote control switch, receiver module, motorcycles, automobile anti-theft products, home security products, electric doors, shutter doors, windows, remote control socket, remote control LED, remote audio remote control electric doors, garage door remote control, remote control retractable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
  FS1000A - 433Mhz RF Transmitter: This is 433Mhz RF transmitter with receiver kit for Arduino ARM MCU wireless Application environment: Remote control switch, receiver module, motorcycles, automobile anti-theft products, home security products, electric doors, shutter doors, windows, remote control socket, remote control LED, remote audio remote control electric doors, garage door remote control, remote control retractable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
